# Fritzing sketch Seatalk (saved by Fritzing 0.7.4b)
stripboards: 1

parts:
  Q1 = NPN-Transistor [part_number="BC237 or equiv" package="TO92 [THT]"]
  Q2 = PNP-Transistor [part_number="BC212 or equiv" package="TO92 [THT]"]
  R1 = Resistor [tolerance=±5% resistance=10k package=THT]
  J1 = female pin header, 1 pin [form="♀ (female)" part_number="Seatalk yellow"]
  J2 = female pin header, 1 pin [form="♀ (female)" part_number="Seatalk red"]
  J3 = female pin header, 1 pin [form="♀ (female)" part_number="Seatalk grey"]
  J5 = female pin header, 1 pin [form="♀ (female)" part_number="RS232 TX"]
  J6 = female pin header, 1 pin [form="♀ (female)" part_number="RS232 GND"]
  R3 = Resistor [tolerance=±5% resistance=10k package=THT]
  R4 = Resistor [tolerance=±5% resistance=6.8k package=THT]
  R5 = Resistor [tolerance=±5% resistance=2.2k package=THT]
  R6 = Resistor [tolerance=±5% resistance=3.9k package=THT]
  J4 = female pin header, 1 pin [form="♀ (female)" part_number="RS232 RX"]

nets:
  N1: Q1.E, J3.pin1, J6.pin1, R4.Pin_1, R6.Pin_1
  N2: Q1.B, R3.Pin_1, R6.Pin_0
  N3: Q1.C, R1.Pin_1, J1.pin1
  N4: Q2.E, J2.pin1, R5.Pin_0
  N5: Q2.B, R1.Pin_0, R5.Pin_1
  N6: Q2.C, R4.Pin_0, J4.pin1
  N7: J5.pin1, R3.Pin_0

notes:
  Seatalk Side
  Grey (Gnd)
  Red (+ve)
  Yellow (Data)
  RS232 side
  RX (Blue)
  TX (White)
  GND(Green)
  RS232 to Seatalk
  Data
  GND
  12V+
  TX
  RX
  Based on information from Thomas Knauf http://www.thomasknauf.de/rap/seatalk1.htm#Har
